// Logisim project DM-02.circ as structural Verilog: 13 circuits, main circuit DM-02
module DM_02 (
  input  [7:0] in_1,
  input  [15:0] in_2,
  input  in_3,
  output [4:0] FLAGS__DNZOC,
  output [4:0] out_5,
  output Carry,
  output Overflow,
  output Zero,
  output Negative,
  output [3:0] out_10,
  output [3:0] out_11,
  output [7:0] out_12,
  output [15:0] CONTROLWORD,
  output [3:0] out_14
);

  wire A_clock, ALU_clock, and_2_out, and_3_out, and_4_out, and_6_out, B_clock, button_1_out, C_clock,
       CLOCK1, CLOCK1_EDGE, CLOCK2, CLOCK2_EDGE, clock_1_out, CLOCK_halt, clock_phases_1_halted,
       CONTINUE_out, control_word_decoder_1_cl_fclr_c, control_word_decoder_1_cl_fclr_z,
       control_word_decoder_1_cl_fset_c, control_word_decoder_1_cl_fset_z, control_word_decoder_1_cl_mar_inc,
       control_word_decoder_1_cl_stk_mar_transfer, control_word_decoder_1_ncl_mem_out,
       control_word_decoder_1_ncl_stk_h_load, control_word_decoder_1_ncl_stk_l_load, F_clock, FETCH_0,
       FETCH_1, FETCH_DONE, H_clock, ic_74138_1_p7, ic_74138_1_p8, ic_74138_1_p9, ic_74244_1_p3,
       ic_74244_1_p4, ic_74244_1_p5, ic_74244_1_p6, IO_EN, IR_load, L_clock, MEM_out, n74161_clockfix_1_q1,
       n74161_clockfix_1_q2, n74161_clockfix_1_q3, n74191_bus_2_nrco, n74191_bus_3_nrco, n74191_bus_4_nrco,
       n74191_bus_6_nrco, n74191_bus_7_nrco, n74191_bus_8_nrco, nA_load, nA_out, nALU_load, nALU_out,
       nand_1_out, nand_2_out, nand_3_out, nand_4_out, nand_5_out, nB_load, nB_out, nC_load, nC_out, nCLOCK1,
       nCLOCK1_EDGE, nCLOCK2, nCLOCK2_EDGE, nF_load, nF_out, nFCLR_c, nFCLR_z, nFSET_c, nFSET_z, nH_load,
       nH_out, nL_load, nL_out, nMAR_H_load, nMAR_H_reg_load, nMAR_inc, nMAR_L_load, nMAR_L_reg_load,
       nMEM_load, nMEM_out, nor_2_out, nor_4_out, not_1_out, not_2_out, not_3_out, not_4_out, not_8_out,
       not_9_out, not_10_out, nPC_H_load, nPC_H_out, nPC_L_load, nPC_L_out, nPC_MAR_transfer, nRESET,
       nROM_EN, nSTK_CLK_EN, nSTK_H_out, nSTK_L_out, nSTK_MAR_transfer, or_1_out, or_2_out, or_4_out,
       or_5_out, or_6_out, PC_inc, PC_inc_rom, PC_MAR_transfer, RAM_EN, STK_dec, STK_DOWN_nUP, STK_H_load,
       STK_inc, STK_L_load, TSTATE_MAX, TSTATE_reset, TSTATE_reset_rom;
  wire [3:0] A_p, A_p_2, B_p, B_p_2, C_p, C_p_2, cscvon8_alu_1_p4, cscvon8_alu_1_p4_2, H_p, H_p_2, IR_p,
       IR_p_2, L_p, L_p_2, n74191_bus_1_q, n74191_bus_2_q, n74191_bus_3_q, n74191_bus_4_q, n74191_bus_5_q,
       n74191_bus_6_q, n74377_bus_1_q, n74377_bus_1_q_2, n74377_bus_2_q, n74377_bus_2_q_2, OP_A_q, OP_A_q_2,
       OP_B_q, OP_B_q_2, program_counter_1_peek_l, program_counter_1_peek_l_2, rom_2_data, rom_2_data_2;
  wire [7:0] IO_ADDRESS, OPERATION_q, program_counter_1_peek_h;
  wire [7:5] undriven;

  LED led_1 (.in(clock_phases_1_halted));
  Button button_1 (.out(button_1_out));
  Pull_Resistor pull_resistor_1 (.node(in_1[7]));
  Pull_Resistor pull_resistor_2 (.node(in_1[4]));
  Pull_Resistor pull_resistor_3 (.node(in_1[6]));
  Pull_Resistor pull_resistor_4 (.node(in_1[5]));
  Pull_Resistor pull_resistor_5 (.node(in_1[3]));
  Button CONTINUE (.out(CONTINUE_out));
  Pull_Resistor pull_resistor_6 (.node(in_1[0]));
  Pull_Resistor pull_resistor_7 (.node(in_1[1]));
  Pull_Resistor pull_resistor_8 (.node(in_1[2]));
  Clock clock_1 (.out(clock_1_out));
  or or_1 (or_1_out, button_1_out, CLOCK_halt);
  Hex_Digit_Display hex_digit_display_1 (.value(OP_A_q_2));  // open: dp
  _74377_Bus OP_A (.D(in_1), .CLK(A_clock), .nCE(1'b0), .Q({OP_A_q_2, OP_A_q}));
  not not_1 (not_1_out, nALU_out);
  or or_2 (or_2_out, not_1_out, F_clock);
  // IC_74244 ic_74244_1: pin names not known; wires that end beside it: nALU_load, nF_load, ic_74244_1_p3, ic_74244_1_p4, ic_74244_1_p5, ic_74244_1_p6, ic_74244_1_p3, ic_74244_1_p4, ic_74244_1_p5, ic_74244_1_p6
  nor nor_1 (STK_DOWN_nUP, STK_inc, nor_2_out);
  nor nor_2 (nor_2_out, STK_DOWN_nUP, STK_dec);
  nor nor_3 (nSTK_CLK_EN, STK_dec, STK_inc);
  not not_2 (not_2_out, nRESET);
  nor nor_4 (nor_4_out, not_2_out, TSTATE_reset, TSTATE_MAX);
  not not_3 (not_3_out, FETCH_DONE);
  and and_1 (TSTATE_reset, nCLOCK2_EDGE, TSTATE_reset_rom);
  Clock_Phases clock_phases_1 (
    .CLOCK(clock_1_out), .HALT(or_1_out), .CONTINUE(CONTINUE_out), .HALTED(clock_phases_1_halted),
    .nCLOCK2(nCLOCK2), .CLOCK1(CLOCK1), .nCLOCK1(nCLOCK1), .CLOCK2(CLOCK2), .nCLOCK2_EDGE(nCLOCK2_EDGE),
    .nCLOCK1_EDGE(nCLOCK1_EDGE), .CLOCK1_EDGE(CLOCK1_EDGE), .CLOCK2_EDGE(CLOCK2_EDGE));
  Hex_Digit_Display hex_digit_display_2 (.value(OP_A_q));  // open: dp
  nand nand_1 (nand_1_out, STK_H_load, CLOCK2);
  nand nand_2 (nand_2_out, CLOCK2, STK_L_load);
  and and_2 (and_2_out, nor_4_out, not_3_out);
  Hex_Digit_Display hex_digit_display_3 (.value(A_p));  // open: dp
  Hex_Digit_Display hex_digit_display_4 (.value(A_p_2));  // open: dp
  _74574_Peek A (.nOE(nA_out), .CLK(A_clock), .D(in_1), .Q(in_1), .P({A_p_2, A_p}));
  Hex_Digit_Display hex_digit_display_5 (.value(OP_B_q_2));  // open: dp
  // DIP_7474 dip_7474_1: pin names not known; wires that end beside it: nFCLR_c, ic_74244_1_p3, or_2_out, nFSET_c, Carry, nFCLR_z, nFSET_z, ic_74244_1_p5, or_2_out, out_11[2]
  Hex_Digit_Display hex_digit_display_6 (.value(n74191_bus_1_q));  // open: dp
  _74161_Clockfix u_74161_clockfix_1 (
    .CLK(and_3_out), .nCLR(nor_4_out), .nPE(1'b1), .CEP(1'b1), .CET(1'b1), .Q1(n74161_clockfix_1_q1),
    .Q2(n74161_clockfix_1_q2), .Q3(n74161_clockfix_1_q3));  // open: D1, D4, Q4, TC, D3, D2
  and and_3 (and_3_out, and_2_out, CLOCK1);
  Hex_Digit_Display hex_digit_display_7 (.value(OP_B_q));  // open: dp
  _74377_Bus OP_B (.D(in_1), .CLK(ALU_clock), .nCE(1'b0), .Q({OP_B_q_2, OP_B_q}));
  Hex_Digit_Display hex_digit_display_8 (.value(n74191_bus_2_q));  // open: dp
  Hex_Digit_Display hex_digit_display_9 (.value(n74191_bus_3_q));  // open: dp
  _74191_Bus u_74191_bus_1 (
    .nU_D(STK_DOWN_nUP), .CK(n74191_bus_2_nrco), .nCTEN(nSTK_CLK_EN), .nPL(nand_1_out), .Q(n74191_bus_1_q),
    .D(in_1[7:4]));  // open: TC, nRCO
  not not_4 (not_4_out, TSTATE_reset);
  and and_4 (and_4_out, not_4_out, FETCH_DONE);
  Hex_Digit_Display hex_digit_display_10 (.value(in_1[3:0]));  // open: dp
  Hex_Digit_Display hex_digit_display_11 (.value(in_1[7:4]));  // open: dp
  Hex_Digit_Display hex_digit_display_12 (.value(B_p_2));  // open: dp
  _74574_Peek B (.nOE(nB_out), .CLK(B_clock), .D(in_1), .Q(in_1), .P({B_p_2, B_p}));
  _74377_Bus OPERATION (.D({undriven, out_5}), .CLK(ALU_clock), .nCE(1'b0), .Q(OPERATION_q));
  Hex_Digit_Display hex_digit_display_13 (.value(n74191_bus_4_q));  // open: dp
  _74191_Bus u_74191_bus_2 (
    .nU_D(STK_DOWN_nUP), .CK(n74191_bus_3_nrco), .nCTEN(nSTK_CLK_EN), .nPL(nand_1_out),
    .nRCO(n74191_bus_2_nrco), .Q(n74191_bus_2_q), .D(in_1[3:0]));  // open: TC
  // IC_74138 ic_74138_1: pin names not known; wires that end beside it: n74161_clockfix_1_q1, n74161_clockfix_1_q2, n74161_clockfix_1_q3, 1'b0, 1'b0, nRESET, ic_74138_1_p7, ic_74138_1_p8, ic_74138_1_p9
  not not_5 (FETCH_0, ic_74138_1_p7);
  not not_6 (FETCH_1, ic_74138_1_p8);
  not not_7 (FETCH_DONE, ic_74138_1_p9);
  _74161_Bus u_74161_bus_1 (
    .CLK(CLOCK1), .nCLR(and_4_out), .nPE(1'b1), .CEP(1'b1), .CET(1'b1), .Q(out_10), .TC(TSTATE_MAX));  // open: D
  Hex_Digit_Display hex_digit_display_14 (.value(B_p));  // open: dp
  // CSCvon8_ALU cscvon8_alu_1: pin names not known; wires that end beside it: {OP_B_q_2, OP_B_q}, {OP_A_q_2, OP_A_q}, OPERATION_q[4:0], {cscvon8_alu_1_p4_2, cscvon8_alu_1_p4}, FLAGS__DNZOC, 1'b1
  // DIP_7474 dip_7474_2: pin names not known; wires that end beside it: 1'b1, ic_74244_1_p4, or_2_out, 1'b1, out_11[1], 1'b1, 1'b1, ic_74244_1_p6, or_2_out, Negative
  Pull_Resistor pull_resistor_9 (.node(TSTATE_MAX));
  Hex_Digit_Display hex_digit_display_15 (.value(in_2[15:12]));  // open: dp
  Hex_Digit_Display hex_digit_display_16 (.value(in_2[11:8]));  // open: dp
  Hex_Digit_Display hex_digit_display_17 (.value(C_p_2));  // open: dp
  _74574_Peek C (.nOE(nC_out), .CLK(C_clock), .D(in_1), .Q(in_1), .P({C_p_2, C_p}));
  Hex_Digit_Display hex_digit_display_18 (.value(cscvon8_alu_1_p4));  // open: dp
  Hex_Digit_Display hex_digit_display_19 (.value(cscvon8_alu_1_p4_2));  // open: dp
  Pull_Resistor pull_resistor_10 (.node(Negative));
  _74245_Bus u_74245_bus_1 (.A({n74191_bus_3_q, n74191_bus_4_q}), .nOE(nSTK_L_out), .B(in_1));
  _74245_Bus u_74245_bus_2 (.A({n74191_bus_1_q, n74191_bus_2_q}), .nOE(nSTK_H_out), .B(in_1));
  _74245_Bus u_74245_bus_3 (.A({n74191_bus_3_q, n74191_bus_4_q}), .nOE(nSTK_MAR_transfer), .B(in_2[7:0]));
  _74245_Bus u_74245_bus_4 (.A({n74191_bus_1_q, n74191_bus_2_q}), .nOE(nSTK_MAR_transfer), .B(in_2[15:8]));
  _74191_Bus u_74191_bus_3 (
    .nU_D(STK_DOWN_nUP), .CK(n74191_bus_4_nrco), .nCTEN(nSTK_CLK_EN), .nPL(nand_2_out),
    .nRCO(n74191_bus_3_nrco), .Q(n74191_bus_3_q), .D(in_1[7:4]));  // open: TC
  Hex_Digit_Display hex_digit_display_20 (.value(in_2[7:4]));  // open: dp
  Hex_Digit_Display hex_digit_display_21 (.value(in_2[3:0]));  // open: dp
  Hex_Digit_Display hex_digit_display_22 (.value(C_p));  // open: dp
  Pull_Resistor pull_resistor_11 (.node(out_11[1]));
  Pull_Resistor pull_resistor_12 (.node(out_11[2]));
  Pull_Resistor pull_resistor_13 (.node(Carry));
  _74191_Bus u_74191_bus_4 (
    .nU_D(STK_DOWN_nUP), .CK(CLOCK2), .nCTEN(nSTK_CLK_EN), .nPL(nand_2_out), .nRCO(n74191_bus_4_nrco),
    .Q(n74191_bus_4_q), .D(in_1[3:0]));  // open: TC
  Hex_Digit_Display hex_digit_display_23 (.value(H_p_2));  // open: dp
  _74574_Peek H (.nOE(nH_out), .CLK(H_clock), .D(in_1), .Q(in_1), .P({H_p_2, H_p}));
  _74245_Bus u_74245_bus_5 (.A({cscvon8_alu_1_p4_2, cscvon8_alu_1_p4}), .nOE(nALU_out), .B(in_1));
  nor nor_5 (nPC_MAR_transfer, FETCH_0, PC_MAR_transfer);
  nor nor_6 (nMEM_out, FETCH_1, MEM_out);
  and and_5 (IR_load, FETCH_1, CLOCK2);
  Hex_Digit_Display hex_digit_display_24 (.value(H_p));  // open: dp
  or or_3 (PC_inc, IR_load, PC_inc_rom);
  Hex_Digit_Display hex_digit_display_25 (.value(L_p_2));  // open: dp
  _74574_Peek L (.nOE(nL_out), .CLK(L_clock), .D(in_1), .Q(in_1), .P({L_p_2, L_p}));
  _74245_Bus u_74245_bus_6 (.A(in_1), .nOE(nMAR_L_load), .B(in_2[7:0]));
  _74245_Bus u_74245_bus_7 (.A(in_1), .nOE(nMAR_H_load), .B(in_2[15:8]));
  Hex_Digit_Display hex_digit_display_26 (.value(L_p));  // open: dp
  and and_6 (and_6_out, nPC_MAR_transfer, nSTK_MAR_transfer);
  Hex_Digit_Display hex_digit_display_27 (.value(IR_p_2));  // open: dp
  _74574_Peek IR (.nOE(1'b0), .CLK(IR_load), .D(in_1), .Q(out_12), .P({IR_p_2, IR_p}));
  or or_4 (or_4_out, nMAR_H_reg_load, nCLOCK2);
  or or_5 (or_5_out, nCLOCK2, nMAR_L_reg_load);
  and and_7 (nMAR_H_reg_load, nMAR_H_load, and_6_out);
  and and_8 (nMAR_L_reg_load, and_6_out, nMAR_L_load);
  Hex_Digit_Display hex_digit_display_28 (.value(IR_p));  // open: dp
  Pull_Resistor pull_resistor_14 (.node(out_12[7]));
  Pull_Resistor pull_resistor_15 (.node(out_12[6]));
  not not_8 (not_8_out, nPC_MAR_transfer);
  Hex_Digit_Display hex_digit_display_29 (.value(n74191_bus_5_q));  // open: dp
  Hex_Digit_Display hex_digit_display_30 (.value(n74191_bus_6_q));  // open: dp
  _74191_Bus u_74191_bus_5 (
    .nU_D(1'b0), .CK(n74191_bus_6_nrco), .nCTEN(nMAR_inc), .nPL(or_4_out), .Q(n74191_bus_5_q), .D(in_2[15:12]));  // open: TC, nRCO
  Pull_Resistor pull_resistor_16 (.node(out_12[5]));
  Pull_Resistor pull_resistor_17 (.node(out_12[0]));
  Pull_Resistor pull_resistor_18 (.node(out_12[3]));
  Pull_Resistor pull_resistor_19 (.node(out_12[4]));
  Pull_Resistor pull_resistor_20 (.node(out_12[1]));
  Pull_Resistor pull_resistor_21 (.node(out_12[2]));
  nand nand_3 (nand_3_out, not_8_out, CLOCK1);
  Hex_Digit_Display hex_digit_display_31 (.value(IO_ADDRESS[3:0]));  // open: dp
  Hex_Digit_Display hex_digit_display_32 (.value(IO_ADDRESS[7:4]));  // open: dp
  _74191_Bus u_74191_bus_6 (
    .nU_D(1'b0), .CK(n74191_bus_7_nrco), .nCTEN(nMAR_inc), .nPL(or_4_out), .nRCO(n74191_bus_6_nrco),
    .Q(n74191_bus_6_q), .D(in_2[11:8]));  // open: TC
  Program_Counter program_counter_1 (
    .INCREMENT(PC_inc), .nRESET(nRESET), .CLOCK(nCLOCK1), .nH_load(nPC_H_load), .nL_load(nPC_L_load),
    .nH_out(nPC_H_out), .nL_out(nPC_L_out), .nADDRESS_out(nand_3_out), .DATA_BUS_IN(in_1),
    .PEEK_H(program_counter_1_peek_h), .PEEK_L({program_counter_1_peek_l_2, program_counter_1_peek_l}),
    .DATA_BUS_OUT(in_1), .ADDRESS_BUS_OUT(in_2));
  Hex_Digit_Display hex_digit_display_33 (.value(out_12[7:4]));  // open: dp
  Pull_Resistor pull_resistor_22 (.node(out_10[0]));
  Pull_Resistor pull_resistor_23 (.node(out_10[1]));
  Pull_Resistor pull_resistor_24 (.node(out_10[2]));
  Pull_Resistor pull_resistor_25 (.node(out_10[3]));
  Hex_Digit_Display hex_digit_display_34 (.value(program_counter_1_peek_h[3:0]));  // open: dp
  Hex_Digit_Display hex_digit_display_35 (.value(program_counter_1_peek_h[7:4]));  // open: dp
  _74191_Bus u_74191_bus_7 (
    .nU_D(1'b0), .CK(n74191_bus_8_nrco), .nCTEN(nMAR_inc), .nPL(or_5_out), .nRCO(n74191_bus_7_nrco),
    .Q(IO_ADDRESS[7:4]), .D(in_2[7:4]));  // open: TC
  Hex_Digit_Display hex_digit_display_36 (.value(out_12[3:0]));  // open: dp
  Hex_Digit_Display hex_digit_display_37 (.value(out_10));  // open: dp
  not not_9 (not_9_out, nCLOCK2_EDGE);
  Hex_Digit_Display hex_digit_display_38 (.value(program_counter_1_peek_l));  // open: dp
  Hex_Digit_Display hex_digit_display_39 (.value(program_counter_1_peek_l_2));  // open: dp
  _74191_Bus u_74191_bus_8 (
    .nU_D(1'b0), .CK(nCLOCK2), .nCTEN(nMAR_inc), .nPL(or_5_out), .nRCO(n74191_bus_8_nrco),
    .Q(IO_ADDRESS[3:0]), .D(in_2[3:0]));  // open: TC
  Hex_Digit_Display hex_digit_display_40 (.value({Negative, out_11[2:1], Carry}));  // open: dp
  ROM #(.addrWidth(16), .dataWidth(16)) rom_1 (
    .addr({out_12, out_10, Negative, out_11[2:1], Carry}), .data(CONTROLWORD), .sel(FETCH_DONE));
  Pull_Resistor pull_resistor_26 (.node(B_clock));
  Pull_Resistor pull_resistor_27 (.node(C_clock));
  Pull_Resistor pull_resistor_28 (.node(H_clock));
  Pull_Resistor pull_resistor_29 (.node(A_clock));
  _74240 u_74240_1 (
    .A1(nA_load), .A2(nB_load), .A3(nC_load), .A4(nH_load), .nOEA(not_9_out), .B1(nL_load), .B2(nALU_load),
    .B3(nF_load), .nOEB(not_9_out), .Y1(A_clock), .Y2(B_clock), .Y3(C_clock), .Y4(H_clock), .Z1(L_clock),
    .Z2(ALU_clock), .Z3(F_clock));  // open: B4, Z4
  Pull_Resistor pull_resistor_30 (.node(CONTROLWORD));
  Pull_Resistor pull_resistor_31 (.node(F_clock));
  Pull_Resistor pull_resistor_32 (.node(L_clock));
  Pull_Resistor pull_resistor_33 (.node(ALU_clock));
  not not_10 (not_10_out, nROM_EN);
  or or_6 (or_6_out, n74191_bus_5_q[2], n74191_bus_5_q[3]);
  Hex_Digit_Display hex_digit_display_41 (.value(rom_2_data_2));  // open: dp
  ROM #(.addrWidth(16)) rom_2 (
    .addr({n74191_bus_5_q, n74191_bus_6_q, IO_ADDRESS}), .data({rom_2_data_2, rom_2_data}), .sel(not_10_out));
  RAM #(.addrWidth(16)) ram_1 (
    .addr({n74191_bus_5_q, n74191_bus_6_q, IO_ADDRESS}), .data({rom_2_data_2, rom_2_data}), .sel(RAM_EN),
    .clk(nCLOCK1), .ld(nMEM_load));  // open: clr
  and and_9 (IO_EN, n74191_bus_6_q[0], n74191_bus_6_q[1], n74191_bus_6_q[2], n74191_bus_6_q[3], n74191_bus_5_q[0], n74191_bus_5_q[1], n74191_bus_5_q[2], n74191_bus_5_q[3]);
  nand nand_4 (nand_4_out, or_6_out, nand_5_out);
  nand nand_5 (nand_5_out, IO_EN, IO_EN);
  or or_7 (nROM_EN, IO_EN, RAM_EN);
  not not_11 (STK_H_load, control_word_decoder_1_ncl_stk_h_load);
  not not_12 (STK_L_load, control_word_decoder_1_ncl_stk_l_load);
  not not_13 (MEM_out, control_word_decoder_1_ncl_mem_out);
  Hex_Digit_Display hex_digit_display_42 (.value(rom_2_data));  // open: dp
  nand nand_6 (RAM_EN, nand_4_out, nand_4_out);
  Control_Word_Decoder control_word_decoder_1 (
    .CONTROL_WORD(CONTROLWORD), .nCL_A_load(nA_load), .CL_TSTATE_reset(TSTATE_reset_rom),
    .nCL_B_load(nB_load), .nCL_C_load(nC_load), .CL_CLOCK_halt(CLOCK_halt), .nCL_H_load(nH_load),
    .CL_STK_inc(STK_inc), .nCL_L_load(nL_load), .nCL_ALU_load(nALU_load), .CL_STK_dec(STK_dec),
    .nCL_F_load(nF_load), .CL_PC_inc(PC_inc_rom), .nCL_MAR_H_load(nMAR_H_load), .nCL_MAR_L_load(nMAR_L_load),
    .CL_PC_MAR_transfer(PC_MAR_transfer), .nCL_MEM_load(nMEM_load),
    .CL_STK_MAR_transfer(control_word_decoder_1_cl_stk_mar_transfer), .nCL_PC_H_load(nPC_H_load),
    .nCL_PC_L_load(nPC_L_load), .nCL_STK_H_load(control_word_decoder_1_ncl_stk_h_load),
    .nCL_STK_L_load(control_word_decoder_1_ncl_stk_l_load), .CL_MAR_inc(control_word_decoder_1_cl_mar_inc),
    .nCL_A_out(nA_out), .CL_FSET_z(control_word_decoder_1_cl_fset_z), .nCL_B_out(nB_out),
    .CL_FSET_c(control_word_decoder_1_cl_fset_c), .nCL_C_out(nC_out), .nCL_H_out(nH_out),
    .CL_FCLR_z(control_word_decoder_1_cl_fclr_z), .nCL_L_out(nL_out),
    .CL_FCLR_c(control_word_decoder_1_cl_fclr_c), .nCL_F_out(nF_out),
    .nCL_MEM_out(control_word_decoder_1_ncl_mem_out), .nCL_PC_H_out(nPC_H_out), .nCL_PC_L_out(nPC_L_out),
    .nCL_STK_H_out(nSTK_H_out), .nCL_STK_L_out(nSTK_L_out), .OE(FETCH_DONE), .ALU_OP(out_5),
    .nCL_ALU_out(nALU_out));
  _74245_Bus u_74245_bus_8 (.A({rom_2_data_2, rom_2_data}), .nOE(nMEM_out), .B(in_1));
  _74245_Bus u_74245_bus_9 (.A(in_1), .nOE(nMEM_load), .B({rom_2_data_2, rom_2_data}));
  not not_14 (nSTK_MAR_transfer, control_word_decoder_1_cl_stk_mar_transfer);
  not not_15 (nMAR_inc, control_word_decoder_1_cl_mar_inc);
  not not_16 (nFSET_z, control_word_decoder_1_cl_fset_z);
  not not_17 (nFSET_c, control_word_decoder_1_cl_fset_c);
  not not_18 (nFCLR_z, control_word_decoder_1_cl_fclr_z);
  not not_19 (nFCLR_c, control_word_decoder_1_cl_fclr_c);
  not not_20 (nRESET, in_3);
  _74245_Bus u_74245_bus_10 (.A(in_1), .nOE(nMAR_L_load), .B(in_2[7:0]));
  _74245_Bus u_74245_bus_11 (.A(in_1), .nOE(nMAR_H_load), .B(in_2[15:8]));
  Hex_Digit_Display hex_digit_display_43 (.value(n74377_bus_2_q_2));  // open: dp
  Hex_Digit_Display hex_digit_display_44 (.value(n74377_bus_2_q));  // open: dp
  Hex_Digit_Display hex_digit_display_45 (.value(n74377_bus_1_q_2));  // open: dp
  Hex_Digit_Display hex_digit_display_46 (.value(n74377_bus_1_q));  // open: dp
  _74377_Bus u_74377_bus_1 (.D(in_2[7:0]), .CLK(CLOCK2), .nCE(nMAR_L_reg_load), .Q({n74377_bus_1_q_2, n74377_bus_1_q}));
  _74377_Bus u_74377_bus_2 (
    .D(in_2[15:8]), .CLK(CLOCK2), .nCE(nMAR_H_reg_load), .Q({n74377_bus_2_q_2, n74377_bus_2_q}));

  assign {out_11[3], out_11[0]} = {Negative, Carry};
  assign out_14 = out_10;
  assign Overflow = out_11[1];
  assign Zero = out_11[2];

  // Other names for the same wires on the sheet: ALU_OP[4:0] = out_5; Fc = Carry;
  //   FLAGS[3:0] = {Negative, out_11[2:1], Carry}; Fo = out_11[1]; Fz = out_11[2]; Fn = Negative;
  //   TSTATE[3:0] = out_10; INSTRUCTION[7:0] = out_12; ADDRESS[15:0] = in_2; CONTROL_WORD[15:0] = CONTROLWORD;
  //   DATA[7:0] = in_1

  // Notes on the sheet:
  //   STACK POINTER
  //   REGISTERS
  //   FLAGS REGISTER
  //   TODO: Synchronous reset?
  //   STK_H
  //   STK_L
  //   SEQUENCER
  //   FETCH CYCLE
  //   TSTATE COUNTER
  //   ALU
  //   MEMORY ACCESS REGISTER
  //   MAR_H
  //   MAR_L
  //   PC_H
  //   MICROCODE ROM
  //   PC_L
  //   contents of rom_1 (hex, n*v repeats v):
  //   16*800 240*0 16*9080 16*800 224*0 16*9880 16*800 224*0 16*a080 16*800 224*0 16*a880 16*800 224*0
  //   16*8900 16*800 224*0 16*9900 16*800 224*0 16*a100 16*800 224*0 16*a900 16*800 224*0 16*8980 16*800
  //   224*0 16*9180 16*800 224*0 16*a180 16*800 224*0 16*a980 16*800 224*0 16*8a00 16*800 224*0 16*9200
  //   16*800 224*0 16*9a00 16*800 224*0 16*aa00 16*800 224*0 16*8a80 16*800 224*0 16*9280 16*800 224*0
  //   16*9a80 16*800 224*0 16*a280 16*800 224*0 16*a100 16*a980 16*800 208*0 16*9200 16*9a80 16*800 208*0
  //   16*d08c 16*2802 224*0 16*d10c 16*2802 224*0 16*d18c 16*2802 224*0 16*d20c 16*2802 224*0 16*d28c
  //   16*2802 224*0 16*d10c 16*2800 16*d18c 16*2802 192*0 16*d20c 16*2800 16*d28c 16*2802 192*0 16*d20c
  //   16*2800 16*d28c 16*a400 16*ac80 16*d080 16*2802 144*0 16*d20c 16*2800 16*d28c 16*a400 16*ac80
  //   16*d100 16*2802 144*0 16*d20c 16*2800 16*d28c 16*a400 16*ac80 16*d180 16*2802 144*0 16*d20c 16*2800
  //   16*d28c 16*a400 16*ac80 16*d100 16*4000 16*d180 16*2802 112*0 16*d20c 16*2800 16*d28c 16*a400
  //   16*ac80 16*d200 16*4000 16*d280 16*2802 112*0 16*d20c 16*2800 16*d28c 16*a400 16*ac80 16*8d00
  //   16*2802 144*0 16*d20c 16*2800 16*d28c 16*a400 16*ac80 16*9500 16*2802 144*0 16*d20c 16*2800 16*d28c
  //   16*a400 16*ac80 16*9d00 16*2802 144*0 16*d20c 16*2800 16*d28c 16*a400 16*ac80 16*9500 16*4000
  //   16*9d00 16*2802 112*0 16*d10c 16*2800 16*d18c 16*9400 16*9c80 16*a500 16*4000 16*ad00 16*2802 112*0
  //   16*d20c 16*2800 16*d28c 16*a400 16*ac80 16*d200 16*4000 16*d280 16*a400 16*ac80 16*d080 16*2802 64*0
  //   16*d20c 16*2800 16*d28c 16*a400 16*ac80 16*d200 16*4000 16*d280 16*a400 16*ac80 16*d100 16*2802 64*0
  //   16*d20c 16*2800 16*d28c 16*a400 16*ac80 16*d200 16*4000 16*d280 16*a400 16*ac80 16*d180 16*2802 64*0
  //   16*d20c 16*2800 16*d28c 16*a400 16*ac80 16*d200 16*4000 16*d280 16*a400 16*ac80 16*d100 16*4000
  //   16*d180 16*2802 32*0 16*d20c 16*2800 16*d28c 16*a400 16*ac80 16*d200 16*4000 16*d280 16*a400 16*ac80
  //   16*8d00 16*2802 64*0 16*d20c 16*2800 16*d28c 16*a400 16*ac80 16*d200 16*4000 16*d280 16*a400 16*ac80
  //   16*9500 16*2802 64*0 16*d20c 16*2800 16*d28c 16*a400 16*ac80 16*d200 16*4000 16*d280 16*a400 16*ac80
  //   16*9d00 16*2802 64*0 16*d20c 16*2800 16*d28c 16*a400 16*ac80 16*d200 16*4000 16*d280 16*a400 16*ac80
  //   16*9500 16*4000 16*9d00 16*2802 32*0 16*9400 16*9c80 16*d080 16*800 192*0 16*9400 16*9c80 16*d200
  //   16*800 192*0 16*9400 16*9c80 16*d280 16*800 192*0 16*a400 16*ac80 16*d080 16*800 192*0 16*a400
  //   16*ac80 16*d100 16*800 192*0 16*a400 16*ac80 16*d180 16*800 192*0 16*9400 16*9c80 16*8d00 16*800
  //   192*0 16*9400 16*9c80 16*a500 16*800 192*0 16*9400 16*9c80 16*ad00 16*800 192*0 16*a400 16*ac80
  //   16*8d00 16*800 192*0 16*a400 16*ac80 16*9500 16*800 192*0 16*a400 16*ac80 16*9d00 16*800 192*0
  //   16*9400 16*9c80 16*d100 16*4000 16*d180 16*800 160*0 16*a400 16*ac80 16*d100 16*4000 16*d180 16*800
  //   160*0 16*9400 16*9c80 16*d200 16*4000 16*d280 16*800 160*0 16*a400 16*ac80 16*d200 16*4000 16*d280
  //   16*800 160*0 16*a400 16*ac80 16*9500 16*4000 16*9d00 16*800 160*0 16*9400 16*9c80 16*a500 16*4000
  //   16*ad00 16*800 4256*0 16*8b52 16*b080 16*800 208*0 16*9352 16*b080 16*800 208*0 16*9b52 16*b080
  //   16*800 208*0 16*a352 16*b080 16*800 208*0 16*ab52 16*b080 16*800 208*0 16*3000 16*d352 16*b080
  //   16*2802 3264*0 16*8b56 16*b080 16*800 208*0 16*9356 16*b080 16*800 208*0 16*9b56 16*b080 16*800
  //   208*0 16*a356 16*b080 16*800 208*0 16*ab56 16*b080 16*800 26832*0 16*300a 16*d200 16*3000 16*d280
  //   16*a580 16*ae0a 16*800 144*0 2800 300a 2800 300a 2800 300a 2800 300a 2800 300a 2800 300a 2800 300a
  //   2800 300a 2802 d200 2802 d200 2802 d200 2802 d200 2802 d200 2802 d200 2802 d200 2802 d200 0 3000 0
  //   3000 0 3000 0 3000 0 3000 0 3000 0 3000 0 3000 0 d280 0 d280 0 d280 0 d280 0 d280 0 d280 0 d280 0
  //   d280 0 a580 0 a580 0 a580 0 a580 0 a580 0 a580 0 a580 0 a580 0 ae0a 0 ae0a 0 ae0a 0 ae0a 0 ae0a 0
  //   ae0a 0 ae0a 0 ae0a 0 800 0 800 0 800 0 800 0 800 0 800 0 800 0 800 144*0 4*2800 4*300a 4*2800 4*300a
  //   4*2802 4*d200 4*2802 4*d200 4*0 4*3000 4*0 4*3000 4*0 4*d280 4*0 4*d280 4*0 4*a580 4*0 4*a580 4*0
  //   4*ae0a 4*0 4*ae0a 4*0 4*800 4*0 4*800 144*0 8*2800 8*300a 8*2802 8*d200 8*0 8*30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
  //   MEMORY
  //   contents of rom_2 (hex, n*v repeats v):
  //   1c aa bb 2f 0 10 f0 9*0 40 10 238*0 16*80 16*0 aa bb 222*0 16*80 240*0 16*80 240*0 16*80 1264*0
  //   16*80 240*0 16*80 240*0 16*80 240*0 16*80 1264*0 16*80 240*0 16*80 240*0 16*80 240*0 16*80 256*0
  //   16*80 240*0 16*80 224*0 16*8c 16*2 224*0 16*c 16*2 224*0 16*8c 16*2 224*0 16*c 16*2 224*0 16*8c 16*2
  //   used NAND to bring down no. of chips
  //   Replace OR gates with diode logic?
  //   CONTROL WORD DECODING
  //   MAR_H
  //   MAR_L
endmodule

// CLOCK
module Clock_Phases (
  input  CLOCK,
  input  HALT,
  input  CONTINUE,
  output HALTED,
  output CLOCK1,
  output CLOCK2,
  output nCLOCK1,
  output nCLOCK2,
  output nCLOCK1_EDGE,
  output CLOCK1_EDGE,
  output nCLOCK2_EDGE,
  output CLOCK2_EDGE
);

  wire and_1_out, d_ff_4_q, not_1_out;

  not not_1 (not_1_out, HALTED);
  D_Flip_Flop d_ff_1 (.clk(and_1_out), .D(HALT), .Q(HALTED), .reset(CONTINUE));  // open: Qn, preset, en
  and and_1 (and_1_out, CLOCK, not_1_out);
  D_Flip_Flop d_ff_2 (.clk(and_1_out), .D(1'b1), .Q(CLOCK1), .Qn(nCLOCK1), .reset(d_ff_4_q));  // open: preset, en
  D_Flip_Flop d_ff_3 (.clk(and_1_out), .D(CLOCK1), .Q(CLOCK2), .Qn(nCLOCK2));  // open: preset, en, reset
  D_Flip_Flop d_ff_4 (.clk(and_1_out), .D(CLOCK2), .Q(d_ff_4_q));  // open: Qn, preset, en, reset
  D_Flip_Flop d_ff_5 (.clk(nCLOCK1), .D(nCLOCK1), .Q(nCLOCK1_EDGE), .reset(nCLOCK2));  // open: Qn, preset, en
  D_Flip_Flop d_ff_6 (.clk(CLOCK1), .D(CLOCK1), .Q(CLOCK1_EDGE), .reset(CLOCK2));  // open: Qn, preset, en
  D_Flip_Flop d_ff_7 (.clk(nCLOCK2), .D(nCLOCK2), .Q(nCLOCK2_EDGE), .reset(CLOCK1));  // open: Qn, preset, en
  D_Flip_Flop d_ff_8 (.clk(CLOCK2), .D(CLOCK2), .Q(CLOCK2_EDGE), .reset(nCLOCK1));  // open: Qn, preset, en

  // Notes on the sheet:
  //   Rising edge trigger for ~CLOCK1
  //   Rising edge trigger for CLOCK1
  //   Rising edge trigger for ~CLOCK2
  //   Rising edge trigger for CLOCK2
endmodule

module LCD_Decoder (
  input  [7:0] DATA,
  input  CLOCK,
  input  nLOAD,
  output RESET,
  output [15:0] COLOR,
  output LCD_CLOCK,
  output [6:0] X_COORD,
  output [6:0] Y_COORD
);

  wire and_1_out, and_3_out, dip_7474_1_p4, n74191_1_p13, n74191_1_p14, n74191_1_p15, n74191_1_p16,
       n74191_2_p13, n74191_3_p13, n74191_3_p14, nand_1_out, not_1_out, not_3_out, not_4_out, RESET_t;
  wire [7:5] ic_74377_1_p16;

  Pull_Resistor pull_resistor_1 (.node(DATA[0]));
  not not_1 (not_1_out, CLOCK);
  // IC_74377 ic_74377_1: pin names not known; wires that end beside it: DATA[0], DATA[1], DATA[2], DATA[3], DATA[4], DATA[5], DATA[6], DATA[7], not_1_out, nLOAD, COLOR[5], COLOR[6], COLOR[7], COLOR[8], COLOR[9], ic_74377_1_p16[5], ic_74377_1_p16[6], ic_74377_1_p16[7]
  and and_1 (and_1_out, ic_74377_1_p16[7], ic_74377_1_p16[6], ic_74377_1_p16[5], COLOR[9], COLOR[8], COLOR[7], COLOR[6], COLOR[5]);
  not not_2 (RESET_t, RESET);
  and and_2 (RESET, and_1_out, not_3_out);
  not not_3 (not_3_out, nLOAD);
  nand nand_1 (nand_1_out, CLOCK, nLOAD);
  and and_3 (and_3_out, CLOCK, not_3_out);
  and and_4 (LCD_CLOCK, RESET_t, dip_7474_1_p4);
  not not_4 (not_4_out, dip_7474_1_p4);
  // DIP_7474 dip_7474_1: pin names not known; wires that end beside it: nand_1_out, and_3_out, and_3_out, dip_7474_1_p4
  // _74191 74191_1: pin names not known; wires that end beside it: 1'b0, not_4_out, 1'b0, RESET_t, X_COORD[0], 1'b0, X_COORD[1], 1'b0, X_COORD[2], 1'b0, X_COORD[3], 1'b0, n74191_1_p13, n74191_1_p14, n74191_1_p15, n74191_1_p16
  // _74191 74191_2: pin names not known; wires that end beside it: 1'b0, n74191_1_p13, 1'b0, RESET_t, X_COORD[4], 1'b0, Y_COORD[0], 1'b0, Y_COORD[1], 1'b0, Y_COORD[2], 1'b0, n74191_2_p13
  // _74191 74191_3: pin names not known; wires that end beside it: 1'b0, n74191_2_p13, 1'b0, RESET_t, Y_COORD[3], 1'b0, Y_COORD[4], 1'b0, n74191_1_p14, 1'b0, n74191_1_p15, 1'b0, n74191_3_p13, n74191_3_p14
  // _74191 74191_4: pin names not known; wires that end beside it: 1'b0, n74191_3_p13, 1'b0, RESET_t, n74191_1_p16, 1'b0, n74191_3_p14, 1'b0, 1'b0, 1'b0

  assign {COLOR[15:10], COLOR[4:0]} = {11{1'b0}};
  assign X_COORD[6:5] = 2'b00;
  assign Y_COORD[6:5] = 2'b00;
endmodule

module _74161_Bus (
  input  CLK,
  input  nCLR,
  input  nPE,
  input  CEP,
  input  CET,
  input  [3:0] D,
  output [3:0] Q,
  output TC
);

  wire and_1_out, and_2_out, and_3_out, and_4_out, and_5_out, and_6_out, and_7_out, and_8_out, and_9_out,
       and_10_out, and_11_out, and_12_out, not_1_out, not_2_out, or_1_out, or_2_out, or_3_out, or_4_out,
       xor_1_out, xor_2_out, xor_3_out, xor_4_out;

  not not_1 (not_1_out, nCLR);
  and and_1 (and_1_out, nPE, CEP, CET);
  not not_2 (not_2_out, nPE);
  and and_2 (and_2_out, D[0], not_2_out);
  and and_3 (and_3_out, Q[0], nPE);
  and and_4 (and_4_out, D[1], not_2_out);
  and and_5 (and_5_out, Q[1], nPE);
  and and_6 (and_6_out, Q[0], and_1_out);
  and and_7 (and_7_out, D[2], not_2_out);
  and and_8 (and_8_out, Q[2], nPE);
  and and_9 (and_9_out, Q[1], Q[0], and_1_out);
  and and_10 (and_10_out, D[3], not_2_out);
  and and_11 (and_11_out, Q[3], nPE);
  and and_12 (and_12_out, Q[2], Q[1], Q[0], and_1_out);
  xor xor_1 (xor_1_out, and_3_out, and_1_out);
  xor xor_2 (xor_2_out, and_5_out, and_6_out);
  xor xor_3 (xor_3_out, and_8_out, and_9_out);
  xor xor_4 (xor_4_out, and_11_out, and_12_out);
  or or_1 (or_1_out, and_2_out, xor_1_out);
  or or_2 (or_2_out, and_4_out, xor_2_out);
  or or_3 (or_3_out, and_7_out, xor_3_out);
  or or_4 (or_4_out, and_10_out, xor_4_out);
  // D_Flip_Flop d_flip_flop_1: pin names not known; wires that end beside it: or_1_out, CLK, not_1_out, Q[0]
  // D_Flip_Flop d_flip_flop_2: pin names not known; wires that end beside it: or_2_out, CLK, not_1_out, Q[1]
  // D_Flip_Flop d_flip_flop_3: pin names not known; wires that end beside it: or_3_out, CLK, not_1_out, Q[2]
  // D_Flip_Flop d_flip_flop_4: pin names not known; wires that end beside it: or_4_out, CLK, not_1_out, Q[3]
  and and_13 (TC, Q[3], Q[2], Q[1], Q[0], CET);
endmodule

// 74161
module _74161_Clockfix (
  input  CLK,
  input  nCLR,
  input  nPE,
  input  CEP,
  input  CET,
  input  D1,
  input  D2,
  input  D3,
  input  D4,
  output Q1,
  output Q2,
  output Q3,
  output Q4,
  output TC
);

  wire and_1_out, and_2_out, and_3_out, and_4_out, and_5_out, and_6_out, and_7_out, and_8_out, and_9_out,
       and_10_out, and_11_out, and_12_out, not_1_out, not_2_out, or_1_out, or_2_out, or_3_out, or_4_out,
       xor_1_out, xor_2_out, xor_3_out, xor_4_out;

  not not_1 (not_1_out, nCLR);
  and and_1 (and_1_out, nPE, CEP, CET);
  not not_2 (not_2_out, nPE);
  and and_2 (and_2_out, D1, not_2_out);
  and and_3 (and_3_out, Q1, nPE);
  and and_4 (and_4_out, D2, not_2_out);
  and and_5 (and_5_out, Q2, nPE);
  and and_6 (and_6_out, Q1, and_1_out);
  and and_7 (and_7_out, D3, not_2_out);
  and and_8 (and_8_out, Q3, nPE);
  and and_9 (and_9_out, Q2, Q1, and_1_out);
  and and_10 (and_10_out, D4, not_2_out);
  and and_11 (and_11_out, Q4, nPE);
  and and_12 (and_12_out, Q3, Q2, Q1, and_1_out);
  xor xor_1 (xor_1_out, and_3_out, and_1_out);
  xor xor_2 (xor_2_out, and_5_out, and_6_out);
  xor xor_3 (xor_3_out, and_8_out, and_9_out);
  xor xor_4 (xor_4_out, and_11_out, and_12_out);
  or or_1 (or_1_out, and_2_out, xor_1_out);
  or or_2 (or_2_out, and_4_out, xor_2_out);
  or or_3 (or_3_out, and_7_out, xor_3_out);
  or or_4 (or_4_out, and_10_out, xor_4_out);
  // D_Flip_Flop d_flip_flop_1: pin names not known; wires that end beside it: or_1_out, CLK, not_1_out, Q1
  // D_Flip_Flop d_flip_flop_2: pin names not known; wires that end beside it: or_2_out, CLK, not_1_out, Q2
  // D_Flip_Flop d_flip_flop_3: pin names not known; wires that end beside it: or_3_out, CLK, not_1_out, Q3
  // D_Flip_Flop d_flip_flop_4: pin names not known; wires that end beside it: or_4_out, CLK, not_1_out, Q4
  and and_13 (TC, Q4, Q3, Q2, Q1, CET);
endmodule

module _74163_Clockfix (
  input  CLK,
  input  CE,
  input  LE,
  input  CEP,
  input  CET,
  input  D1,
  input  D2,
  input  D3,
  input  D4,
  output Q1,
  output Q2,
  output Q3,
  output Q4,
  output TC
);

  wire and_1_out, and_2_out, and_3_out, and_4_out, and_5_out, and_6_out, and_7_out, and_8_out, and_9_out,
       and_10_out, and_11_out, and_12_out, and_13_out, not_1_out, not_2_out, or_1_out, or_2_out, or_3_out,
       or_4_out, xor_1_out, xor_2_out, xor_3_out, xor_4_out;

  not not_1 (not_1_out, CE);
  and and_1 (and_1_out, LE, CEP, CET);
  not not_2 (not_2_out, LE);
  and and_2 (and_2_out, D1, not_1_out, not_2_out);
  and and_3 (and_3_out, Q1, not_1_out, LE);
  and and_4 (and_4_out, not_1_out, and_1_out);
  and and_5 (and_5_out, D2, not_1_out, not_2_out);
  and and_6 (and_6_out, Q2, not_1_out, LE);
  and and_7 (and_7_out, Q1, not_1_out, and_1_out);
  and and_8 (and_8_out, D3, not_1_out, not_2_out);
  and and_9 (and_9_out, Q3, not_1_out, LE);
  and and_10 (and_10_out, Q2, Q1, and_1_out, not_1_out);
  and and_11 (and_11_out, D4, not_1_out, not_2_out);
  and and_12 (and_12_out, Q4, not_1_out, LE);
  and and_13 (and_13_out, Q3, Q2, not_1_out, Q1, and_1_out);
  xor xor_1 (xor_1_out, and_3_out, and_4_out);
  xor xor_2 (xor_2_out, and_6_out, and_7_out);
  xor xor_3 (xor_3_out, and_9_out, and_10_out);
  xor xor_4 (xor_4_out, and_12_out, and_13_out);
  or or_1 (or_1_out, and_2_out, xor_1_out);
  or or_2 (or_2_out, and_5_out, xor_2_out);
  or or_3 (or_3_out, and_8_out, xor_3_out);
  or or_4 (or_4_out, and_11_out, xor_4_out);
  // D_Flip_Flop d_flip_flop_1: pin names not known; wires that end beside it: or_1_out, CLK, Q1
  // D_Flip_Flop d_flip_flop_2: pin names not known; wires that end beside it: or_2_out, CLK, Q2
  // D_Flip_Flop d_flip_flop_3: pin names not known; wires that end beside it: or_3_out, CLK, Q3
  // D_Flip_Flop d_flip_flop_4: pin names not known; wires that end beside it: or_4_out, CLK, Q4
  and and_14 (TC, Q4, Q3, Q2, Q1, CET);
endmodule

// 74191
module _74191_Bus (
  input  nU_D,
  input  CK,
  input  nCTEN,
  input  nPL,
  input  [3:0] D,
  output [3:0] Q,
  output TC,
  output nRCO
);

  wire and_1_out, and_2_out, and_3_out, and_4_out, and_5_out, and_6_out, and_7_out, and_8_out,
       jk_flipflop_1_p4, jk_flipflop_1_p5, jk_flipflop_1_p7, jk_flipflop_2_p4, jk_flipflop_2_p5,
       jk_flipflop_2_p7, jk_flipflop_3_p4, jk_flipflop_3_p7, jk_flipflop_4_p4, jk_flipflop_4_p5, nand_5_out,
       nor_1_out, not_1_out, not_2_out, not_3_out, not_4_out, not_5_out, not_6_out, not_7_out, not_8_out,
       not_9_out, or_1_out, or_2_out, or_3_out;

  not not_1 (not_1_out, nCTEN);
  not not_2 (not_2_out, nU_D);
  // JK_FlipFlop jk_flipflop_1: pin names not known; wires that end beside it: not_1_out, CK, not_1_out, jk_flipflop_1_p4, jk_flipflop_1_p5, Q[0], jk_flipflop_1_p7
  nand nand_1 (jk_flipflop_1_p5, not_3_out, not_4_out);
  not not_3 (not_3_out, nPL);
  not not_4 (not_4_out, D[0]);
  not not_5 (not_5_out, nU_D);
  nand nand_2 (jk_flipflop_1_p4, not_3_out, D[0]);
  and and_1 (and_1_out, Q[0], not_5_out, not_1_out);
  or or_1 (or_1_out, and_1_out, and_2_out);
  and and_2 (and_2_out, nU_D, jk_flipflop_1_p7, not_1_out);
  // JK_FlipFlop jk_flipflop_2: pin names not known; wires that end beside it: or_1_out, CK, or_1_out, jk_flipflop_2_p4, jk_flipflop_2_p5, Q[1], jk_flipflop_2_p7
  nand nand_3 (jk_flipflop_2_p5, not_3_out, not_6_out);
  nand nand_4 (jk_flipflop_2_p4, not_3_out, D[1]);
  not not_6 (not_6_out, D[1]);
  and and_3 (and_3_out, and_1_out, Q[1], not_1_out);
  and and_4 (and_4_out, and_2_out, jk_flipflop_2_p7, not_1_out);
  or or_2 (or_2_out, and_3_out, and_4_out);
  nand nand_5 (nand_5_out, not_3_out, not_7_out);
  // JK_FlipFlop jk_flipflop_3: pin names not known; wires that end beside it: or_2_out, CK, or_2_out, jk_flipflop_3_p4, nand_5_out, Q[2], jk_flipflop_3_p7
  nand nand_6 (jk_flipflop_3_p4, not_3_out, D[2]);
  not not_7 (not_7_out, D[2]);
  and and_5 (and_5_out, and_3_out, Q[2], not_1_out);
  and and_6 (and_6_out, and_4_out, jk_flipflop_3_p7, not_1_out);
  or or_3 (or_3_out, and_5_out, and_6_out);
  // JK_FlipFlop jk_flipflop_4: pin names not known; wires that end beside it: or_3_out, CK, or_3_out, jk_flipflop_4_p4, jk_flipflop_4_p5, Q[3]
  nand nand_7 (jk_flipflop_4_p5, not_3_out, not_8_out);
  not not_8 (not_8_out, D[3]);
  not not_9 (not_9_out, CK);
  nand nand_8 (jk_flipflop_4_p4, not_3_out, D[3]);
  Hex_Digit_Display hex_digit_display_1 (.value(Q));  // open: dp
  nor nor_1 (nor_1_out, Q[3], Q[2], Q[1], Q[0], not_2_out);
  and and_7 (and_7_out, not_2_out, Q[3], Q[2], Q[1], Q[0]);
  or or_4 (TC, nor_1_out, and_7_out);
  and and_8 (and_8_out, TC, not_1_out, not_9_out);
  not not_10 (nRCO, and_8_out);
endmodule

module _74240 (
  input  A1,
  input  A2,
  input  A3,
  input  A4,
  input  nOEA,
  input  B1,
  input  B2,
  input  B3,
  input  B4,
  input  nOEB,
  output Y1,
  output Y2,
  output Y3,
  output Y4,
  output Z1,
  output Z2,
  output Z3,
  output Z4
);

  wire not_1_out, not_2_out;

  not not_1 (not_1_out, nOEA);
  not not_2 (not_2_out, nOEB);
  assign Y1 = not_1_out ? ~A1 : 1'bz;  // Controlled_Inverter controlled_inverter_1
  assign Y2 = not_1_out ? ~A2 : 1'bz;  // Controlled_Inverter controlled_inverter_2
  assign Y3 = not_1_out ? ~A3 : 1'bz;  // Controlled_Inverter controlled_inverter_3
  assign Y4 = not_1_out ? ~A4 : 1'bz;  // Controlled_Inverter controlled_inverter_4
  assign Z1 = not_2_out ? ~B1 : 1'bz;  // Controlled_Inverter controlled_inverter_5
  assign Z2 = not_2_out ? ~B2 : 1'bz;  // Controlled_Inverter controlled_inverter_6
  assign Z3 = not_2_out ? ~B3 : 1'bz;  // Controlled_Inverter controlled_inverter_7
  assign Z4 = not_2_out ? ~B4 : 1'bz;  // Controlled_Inverter controlled_inverter_8
endmodule

// 74245
module _74245_Bus (
  input  [7:0] A,
  input  nOE,
  output [7:0] B
);

  wire not_1_out, not_2_out;

  not not_1 (not_1_out, nOE);
  not not_2 (not_2_out, nOE);
  assign B[0] = not_1_out ? A[0] : 1'bz;  // Controlled_Buffer controlled_buffer_1
  assign B[1] = not_1_out ? A[1] : 1'bz;  // Controlled_Buffer controlled_buffer_2
  assign B[2] = not_1_out ? A[2] : 1'bz;  // Controlled_Buffer controlled_buffer_3
  assign B[3] = not_1_out ? A[3] : 1'bz;  // Controlled_Buffer controlled_buffer_4
  assign B[4] = not_2_out ? A[4] : 1'bz;  // Controlled_Buffer controlled_buffer_5
  assign B[5] = not_2_out ? A[5] : 1'bz;  // Controlled_Buffer controlled_buffer_6
  assign B[6] = not_2_out ? A[6] : 1'bz;  // Controlled_Buffer controlled_buffer_7
  assign B[7] = not_2_out ? A[7] : 1'bz;  // Controlled_Buffer controlled_buffer_8
endmodule

// 74377
module _74377_Bus (
  input  [7:0] D,
  input  CLK,
  input  nCE,
  output [7:0] Q
);

  wire and_1_out, not_1_out;

  not not_1 (not_1_out, nCE);
  and and_1 (and_1_out, CLK, not_1_out);
  // D_Flip_Flop d_flip_flop_1: pin names not known; wires that end beside it: D[0], and_1_out, Q[0]
  // D_Flip_Flop d_flip_flop_2: pin names not known; wires that end beside it: D[1], and_1_out, Q[1]
  // D_Flip_Flop d_flip_flop_3: pin names not known; wires that end beside it: D[2], and_1_out, Q[2]
  // D_Flip_Flop d_flip_flop_4: pin names not known; wires that end beside it: D[3], and_1_out, Q[3]
  // D_Flip_Flop d_flip_flop_5: pin names not known; wires that end beside it: D[4], and_1_out, Q[4]
  // D_Flip_Flop d_flip_flop_6: pin names not known; wires that end beside it: D[5], and_1_out, Q[5]
  // D_Flip_Flop d_flip_flop_7: pin names not known; wires that end beside it: D[6], and_1_out, Q[6]
  // D_Flip_Flop d_flip_flop_8: pin names not known; wires that end beside it: D[7], and_1_out, Q[7]
endmodule

module _74574_Peek (
  input  nOE,
  input  CLK,
  input  [7:0] D,
  output [7:0] P,
  output [7:0] Q
);

  wire not_1_out;

  not not_1 (not_1_out, nOE);
  // D_Flip_Flop d_flip_flop_1: pin names not known; wires that end beside it: D[0], P[0]
  // D_Flip_Flop d_flip_flop_2: pin names not known; wires that end beside it: CLK, D[1], CLK, P[1]
  // D_Flip_Flop d_flip_flop_3: pin names not known; wires that end beside it: D[2], CLK, P[2]
  // D_Flip_Flop d_flip_flop_4: pin names not known; wires that end beside it: D[3], P[3]
  // D_Flip_Flop d_flip_flop_5: pin names not known; wires that end beside it: CLK, D[4], CLK, P[4]
  // D_Flip_Flop d_flip_flop_6: pin names not known; wires that end beside it: D[5], P[5]
  // D_Flip_Flop d_flip_flop_7: pin names not known; wires that end beside it: CLK, D[6], P[6]
  // D_Flip_Flop d_flip_flop_8: pin names not known; wires that end beside it: CLK, D[7], CLK, P[7]
  assign Q[0] = not_1_out ? P[0] : 1'bz;  // Controlled_Buffer controlled_buffer_1
  assign Q[1] = not_1_out ? P[1] : 1'bz;  // Controlled_Buffer controlled_buffer_2
  assign Q[2] = not_1_out ? P[2] : 1'bz;  // Controlled_Buffer controlled_buffer_3
  assign Q[3] = not_1_out ? P[3] : 1'bz;  // Controlled_Buffer controlled_buffer_4
  assign Q[4] = not_1_out ? P[4] : 1'bz;  // Controlled_Buffer controlled_buffer_5
  assign Q[5] = not_1_out ? P[5] : 1'bz;  // Controlled_Buffer controlled_buffer_6
  assign Q[6] = not_1_out ? P[6] : 1'bz;  // Controlled_Buffer controlled_buffer_7
  assign Q[7] = not_1_out ? P[7] : 1'bz;  // Controlled_Buffer controlled_buffer_8

  // Notes on the sheet:
  //   This is the 74x574 chip, but with a PEEK output that always outputs the value stored in ther register
endmodule

module Control_Word_Decoder (
  input  [15:0] CONTROL_WORD,
  input  OE,
  output [4:0] ALU_OP,
  output nCL_A_load,
  output CL_TSTATE_reset,
  output nCL_B_load,
  output nCL_C_load,
  output CL_CLOCK_halt,
  output nCL_H_load,
  output CL_STK_inc,
  output nCL_L_load,
  output nCL_ALU_load,
  output CL_STK_dec,
  output nCL_F_load,
  output CL_PC_inc,
  output nCL_MAR_H_load,
  output nCL_MAR_L_load,
  output CL_PC_MAR_transfer,
  output nCL_MEM_load,
  output CL_STK_MAR_transfer,
  output nCL_PC_H_load,
  output nCL_PC_L_load,
  output nCL_STK_H_load,
  output nCL_STK_L_load,
  output CL_MAR_inc,
  output nCL_A_out,
  output CL_FSET_z,
  output nCL_B_out,
  output CL_FSET_c,
  output nCL_C_out,
  output nCL_H_out,
  output CL_FCLR_z,
  output nCL_L_out,
  output CL_FCLR_c,
  output nCL_ALU_out,
  output nCL_F_out,
  output nCL_MEM_out,
  output nCL_PC_H_out,
  output nCL_PC_L_out,
  output nCL_STK_H_out,
  output nCL_STK_L_out
);

  wire n74154_1_p15, n74154_2_p13, n74154_3_p1, n74154_3_p2, n74154_3_p3, n74154_3_p4, n74154_3_p5,
       n74154_3_p6, n74154_3_p7, n74154_3_p8, n74154_3_p9, n74154_3_p10, n74154_3_p15, n74154_3_p17,
       n74154_3_p18, n74154_4_p2, n74154_4_p3, n74154_4_p4, n74154_4_p5, n74154_4_p6, n74154_4_p7,
       n74154_4_p8, n74154_4_p9, n74154_4_p10, n74154_4_p11, n74154_4_p12, n74154_4_p13, n74154_4_p18,
       n74154_4_p21, n74154_4_p22, not_1_out, not_2_out;

  Pull_Resistor pull_resistor_1 (.node(CONTROL_WORD));
  Pull_Resistor pull_resistor_2 (.node(OE));
  // _74154 74154_1: pin names not known; wires that end beside it: nCL_A_load, nCL_B_load, nCL_C_load, nCL_H_load, nCL_L_load, nCL_ALU_load, nCL_F_load, nCL_MAR_H_load, nCL_MAR_L_load, nCL_MEM_load, CONTROL_WORD[7], CONTROL_WORD[8], CONTROL_WORD[9], CONTROL_WORD[10], n74154_1_p15, n74154_1_p15, nCL_STK_L_load, nCL_STK_H_load, nCL_PC_L_load, nCL_PC_H_load
  // _74154 74154_2: pin names not known; wires that end beside it: nCL_A_out, nCL_B_out, nCL_C_out, nCL_H_out, nCL_L_out, nCL_ALU_out, nCL_F_out, nCL_MEM_out, CONTROL_WORD[11], CONTROL_WORD[12], CONTROL_WORD[13], CONTROL_WORD[14], n74154_2_p13, n74154_2_p13, nCL_STK_L_out, nCL_STK_H_out, nCL_PC_L_out, nCL_PC_H_out
  nand nand_1 (n74154_1_p15, CONTROL_WORD[15], OE);
  nand nand_2 (n74154_2_p13, CONTROL_WORD[15], OE);
  nand nand_3 (CL_TSTATE_reset, n74154_3_p1, n74154_4_p3);
  nand nand_4 (CL_CLOCK_halt, n74154_3_p2, n74154_4_p4);
  nand nand_5 (CL_STK_inc, n74154_3_p3, n74154_4_p5);
  nand nand_6 (CL_STK_dec, n74154_3_p4, n74154_4_p6);
  nand nand_7 (CL_PC_inc, n74154_3_p5, n74154_4_p7);
  nand nand_8 (CL_PC_MAR_transfer, n74154_3_p6, n74154_4_p8);
  nand nand_9 (CL_STK_MAR_transfer, n74154_3_p7, n74154_4_p9);
  nand nand_10 (CL_MAR_inc, n74154_3_p8, n74154_4_p10);
  nand nand_11 (CL_FSET_z, n74154_3_p9, n74154_4_p11);
  nand nand_12 (CL_FSET_c, n74154_3_p10, n74154_4_p12);
  nand nand_13 (CL_FCLR_z, n74154_4_p13, n74154_4_p22);
  nand nand_14 (CL_FCLR_c, n74154_3_p18, n74154_4_p21);
  // _74154 74154_3: pin names not known; wires that end beside it: n74154_3_p1, n74154_3_p2, n74154_3_p3, n74154_3_p4, n74154_3_p5, n74154_3_p6, n74154_3_p7, n74154_3_p8, n74154_3_p9, n74154_3_p10, CONTROL_WORD[1], CONTROL_WORD[2], CONTROL_WORD[3], CONTROL_WORD[4], n74154_3_p15, n74154_3_p15, n74154_3_p17, n74154_3_p18
  // _74154 74154_4: pin names not known; wires that end beside it: n74154_3_p17, n74154_4_p2, n74154_4_p3, n74154_4_p4, n74154_4_p5, n74154_4_p6, n74154_4_p7, n74154_4_p8, n74154_4_p9, n74154_4_p10, n74154_4_p11, n74154_4_p12, n74154_4_p13, CONTROL_WORD[11], CONTROL_WORD[12], CONTROL_WORD[13], CONTROL_WORD[14], n74154_4_p18, n74154_4_p18, n74154_4_p2, n74154_4_p21, n74154_4_p22
  nand nand_15 (n74154_3_p15, not_1_out, OE);
  nand nand_16 (n74154_4_p18, not_2_out, OE);
  not not_1 (not_1_out, CONTROL_WORD[6]);
  not not_2 (not_2_out, CONTROL_WORD[15]);

  assign ALU_OP = CONTROL_WORD[5:1];

  // Other names for the same wires on the sheet: CW_ALU = CONTROL_WORD[6]; CW_OPERATION = CONTROL_WORD[15];
  //   CW_ALU_OP[4:0] = CONTROL_WORD[5:1]; CW_FUNC1[3:0] = CONTROL_WORD[4:1]; CW_OP_LOAD[3:0] = CONTROL_WORD[10:7];
  //   CW_FUNC0[3:0] = CONTROL_WORD[14:11]; CW_OP_OUT[3:0] = CONTROL_WORD[14:11]; OUTPUT_ENABLE = OE

  // Notes on the sheet:
  //   OPERATOR LOAD/OUT
  //   CW_OPERATION=0 (function)
  //   CW_OPERATION=1 (data)
  //   FUNCTIONS
endmodule

module Program_Counter (
  input  INCREMENT,
  input  nRESET,
  input  CLOCK,
  input  nH_load,
  input  nL_load,
  input  nH_out,
  input  nL_out,
  input  nADDRESS_out,
  input  [7:0] DATA_BUS_IN,
  output [7:0] PEEK_H,
  output [7:0] PEEK_L,
  output [7:0] DATA_BUS_OUT,
  output [15:0] ADDRESS_BUS_OUT
);

  wire n74161_bus_2_tc, n74161_bus_3_tc, n74161_bus_4_tc;

  _74161_Bus u_74161_bus_1 (
    .CLK(CLOCK), .nCLR(nRESET), .nPE(nH_load), .CEP(n74161_bus_2_tc), .CET(n74161_bus_2_tc),
    .D(DATA_BUS_IN[7:4]), .Q(PEEK_H[7:4]));  // open: TC
  _74161_Bus u_74161_bus_2 (
    .CLK(CLOCK), .nCLR(nRESET), .nPE(nH_load), .CEP(n74161_bus_3_tc), .CET(n74161_bus_3_tc),
    .D(DATA_BUS_IN[3:0]), .Q(PEEK_H[3:0]), .TC(n74161_bus_2_tc));
  _74161_Bus u_74161_bus_3 (
    .CLK(CLOCK), .nCLR(nRESET), .nPE(nL_load), .CEP(n74161_bus_4_tc), .CET(n74161_bus_4_tc),
    .D(DATA_BUS_IN[7:4]), .Q(PEEK_L[7:4]), .TC(n74161_bus_3_tc));
  _74245_Bus u_74245_bus_1 (.A(PEEK_L), .nOE(nL_out), .B(DATA_BUS_OUT));
  _74245_Bus u_74245_bus_2 (.A(PEEK_H), .nOE(nH_out), .B(DATA_BUS_OUT));
  _74245_Bus u_74245_bus_3 (.A(PEEK_L), .nOE(nADDRESS_out), .B(ADDRESS_BUS_OUT[7:0]));
  _74245_Bus u_74245_bus_4 (.A(PEEK_H), .nOE(nADDRESS_out), .B(ADDRESS_BUS_OUT[15:8]));
  _74161_Bus u_74161_bus_4 (
    .CLK(CLOCK), .nCLR(nRESET), .nPE(nL_load), .CEP(INCREMENT), .CET(1'b1), .D(DATA_BUS_IN[3:0]),
    .Q(PEEK_L[3:0]), .TC(n74161_bus_4_tc));

  // Other names for the same wires on the sheet: INC = INCREMENT

  // Notes on the sheet:
  //   PC_H
  //   PC_L
endmodule
