// Logisim project DM-02.circ as structural Verilog: 5 circuits, main circuit DM-02
module DM_02 (
  input  in_1,
  input  in_2,
  input  in_3,
  input  in_4,
  input  in_5,
  input  in_6,
  input  in_7,
  input  in_8,
  input  in_9,
  input  in_10,
  input  [7:0] in_11,
  input  in_12
);

  wire A_clock, A_out, B_clock, B_out, C_clock, C_out, CLOCK1, CLOCK2, clock_1_out, H_clock, H_out, IR_clock,
       L_clock, L_out, nCLOCK1, nCLOCK2;
  wire [3:0] A_p, A_p_2, B_p, B_p_2, C_p, C_p_2, H_p, H_p_2, IR_p, IR_p_2, L_p, L_p_2;

  Clock clock_1 (.out(clock_1_out));
  Hex_Digit_Display hex_digit_display_1 (.value(A_p_2));  // open: dp
  Clock_Phases clock_phases_1 (
    .CLOCK(clock_1_out), .CLOCK1(CLOCK1), .CLOCK2(CLOCK2), .nCLOCK1(nCLOCK1), .nCLOCK2(nCLOCK2));
  Hex_Digit_Display hex_digit_display_2 (.value(A_p));  // open: dp
  _74574_Peek A (.nOE(A_out), .CLK(A_clock), .D(in_11), .Q(in_11), .P({A_p_2, A_p}));
  Hex_Digit_Display hex_digit_display_3 (.value(B_p_2));  // open: dp
  // CSCvon8_ALU cscvon8_alu_1: pin names not known
  Hex_Digit_Display hex_digit_display_4 (.value(in_11[7:4]));  // open: dp
  Hex_Digit_Display hex_digit_display_5 (.value(B_p));  // open: dp
  _74574_Peek B (.nOE(B_out), .CLK(B_clock), .D(in_11), .Q(in_11), .P({B_p_2, B_p}));
  Hex_Digit_Display hex_digit_display_6 (.value(in_11[3:0]));  // open: dp
  Hex_Digit_Display hex_digit_display_7 (.value(C_p_2));  // open: dp
  Hex_Digit_Display hex_digit_display_8 (.value(C_p));  // open: dp
  _74574_Peek C (.nOE(C_out), .CLK(C_clock), .D(in_11), .Q(in_11), .P({C_p_2, C_p}));
  Hex_Digit_Display hex_digit_display_9 (.value(H_p_2));  // open: dp
  Hex_Digit_Display hex_digit_display_10 (.value(H_p));  // open: dp
  _74574_Peek H (.nOE(H_out), .CLK(H_clock), .D(in_11), .Q(in_11), .P({H_p_2, H_p}));
  Hex_Digit_Display hex_digit_display_11 (.value(L_p_2));  // open: dp
  Hex_Digit_Display hex_digit_display_12 (.value(L_p));  // open: dp
  _74574_Peek L (.nOE(L_out), .CLK(L_clock), .D(in_11), .Q(in_11), .P({L_p_2, L_p}));
  not not_1 (A_out, in_2);
  not not_2 (B_out, in_4);
  not not_3 (C_out, in_6);
  not not_4 (H_out, in_8);
  not not_5 (L_out, in_10);
  Hex_Digit_Display hex_digit_display_13 (.value(IR_p_2));  // open: dp
  Hex_Digit_Display hex_digit_display_14 (.value(IR_p));  // open: dp
  _74574_Peek IR (.nOE(1'b0), .CLK(IR_clock), .P({IR_p_2, IR_p}));  // open: D, Q
  Pull_Resistor pull_resistor_1 (.node(C_clock));
  Pull_Resistor pull_resistor_2 (.node(B_clock));
  Pull_Resistor pull_resistor_3 (.node(A_clock));
  // IC_74244 ic_74244_1: pin names not known; wires that end beside it: in_1, in_3, in_5, in_7, in_9, in_12, CLOCK2, CLOCK2, A_clock, B_clock, C_clock, H_clock, L_clock, IR_clock
  Pull_Resistor pull_resistor_4 (.node(L_clock));
  Pull_Resistor pull_resistor_5 (.node(IR_clock));
  Pull_Resistor pull_resistor_6 (.node(H_clock));

  // Other names for the same wires on the sheet: A_load = in_1; B_load = in_3; C_load = in_5; DATA[7:0] = in_11;
  //   H_load = in_7; IR_load = in_12; L_load = in_9
endmodule

// CLOCK
module Clock_Phases (
  input  CLOCK,
  output CLOCK1,
  output CLOCK2,
  output nCLOCK1,
  output nCLOCK2
);

  wire and_1_out, and_2_out, d_ff_3_q, d_ff_4_q;

  D_Flip_Flop d_ff_1 (.clk(CLOCK), .D(CLOCK), .Q(CLOCK1), .reset(and_1_out));  // open: Qn, preset, en
  D_Flip_Flop d_ff_2 (.clk(CLOCK), .D(CLOCK1), .Q(CLOCK2), .reset(and_2_out));  // open: Qn, preset, en
  not not_1 (nCLOCK1, CLOCK1);
  D_Flip_Flop d_ff_3 (.clk(CLOCK), .D(CLOCK2), .Q(d_ff_3_q), .reset(and_2_out));  // open: Qn, preset, en
  not not_2 (nCLOCK2, CLOCK2);
  and and_1 (and_1_out, CLOCK, d_ff_3_q);
  and and_2 (and_2_out, CLOCK, d_ff_4_q);
  D_Flip_Flop d_ff_4 (.clk(CLOCK), .D(d_ff_3_q), .Q(d_ff_4_q), .reset(and_2_out));  // open: Qn, preset, en
endmodule

module LCD_Decoder (
  input  [7:0] DATA,
  input  CLOCK,
  input  nLOAD,
  output RESET,
  output [15:0] COLOR,
  output LCD_CLOCK,
  output [6:0] X_COORD,
  output [6:0] Y_COORD
);

  wire and_1_out, and_3_out, dip_7474_1_p4, n74191_1_p13, n74191_1_p14, n74191_1_p15, n74191_1_p16,
       n74191_2_p13, n74191_3_p13, n74191_3_p14, nand_1_out, not_1_out, not_3_out, not_4_out, RESET_t;
  wire [7:5] ic_74377_1_p16;

  Pull_Resistor pull_resistor_1 (.node(DATA[0]));
  not not_1 (not_1_out, CLOCK);
  // IC_74377 ic_74377_1: pin names not known; wires that end beside it: DATA[0], DATA[1], DATA[2], DATA[3], DATA[4], DATA[5], DATA[6], DATA[7], not_1_out, nLOAD, COLOR[5], COLOR[6], COLOR[7], COLOR[8], COLOR[9], ic_74377_1_p16[5], ic_74377_1_p16[6], ic_74377_1_p16[7]
  and and_1 (and_1_out, ic_74377_1_p16[7], ic_74377_1_p16[6], ic_74377_1_p16[5], COLOR[9], COLOR[8], COLOR[7], COLOR[6], COLOR[5]);
  not not_2 (RESET_t, RESET);
  and and_2 (RESET, and_1_out, not_3_out);
  not not_3 (not_3_out, nLOAD);
  nand nand_1 (nand_1_out, CLOCK, nLOAD);
  and and_3 (and_3_out, CLOCK, not_3_out);
  and and_4 (LCD_CLOCK, RESET_t, dip_7474_1_p4);
  not not_4 (not_4_out, dip_7474_1_p4);
  // DIP_7474 dip_7474_1: pin names not known; wires that end beside it: nand_1_out, and_3_out, and_3_out, dip_7474_1_p4
  // _74191 74191_1: pin names not known; wires that end beside it: 1'b0, not_4_out, 1'b0, RESET_t, X_COORD[0], 1'b0, X_COORD[1], 1'b0, X_COORD[2], 1'b0, X_COORD[3], 1'b0, n74191_1_p13, n74191_1_p14, n74191_1_p15, n74191_1_p16
  // _74191 74191_2: pin names not known; wires that end beside it: 1'b0, n74191_1_p13, 1'b0, RESET_t, X_COORD[4], 1'b0, Y_COORD[0], 1'b0, Y_COORD[1], 1'b0, Y_COORD[2], 1'b0, n74191_2_p13
  // _74191 74191_3: pin names not known; wires that end beside it: 1'b0, n74191_2_p13, 1'b0, RESET_t, Y_COORD[3], 1'b0, Y_COORD[4], 1'b0, n74191_1_p14, 1'b0, n74191_1_p15, 1'b0, n74191_3_p13, n74191_3_p14
  // _74191 74191_4: pin names not known; wires that end beside it: 1'b0, n74191_3_p13, 1'b0, RESET_t, n74191_1_p16, 1'b0, n74191_3_p14, 1'b0, 1'b0, 1'b0

  assign {COLOR[15:10], COLOR[4:0]} = {11{1'b0}};
  assign X_COORD[6:5] = 2'b00;
  assign Y_COORD[6:5] = 2'b00;
endmodule

// 74161
module _74161_Clockfix (
  input  CLK,
  input  CLR,
  input  LE,
  input  CEP,
  input  CET,
  input  D1,
  input  D2,
  input  D3,
  input  D4,
  output Q1,
  output Q2,
  output Q3,
  output Q4,
  output TC
);

  wire and_1_out, and_2_out, and_3_out, and_4_out, and_5_out, and_6_out, and_7_out, and_8_out, and_9_out,
       and_10_out, and_11_out, and_12_out, not_1_out, not_2_out, or_1_out, or_2_out, or_3_out, or_4_out,
       xor_1_out, xor_2_out, xor_3_out, xor_4_out;

  not not_1 (not_1_out, CLR);
  and and_1 (and_1_out, LE, CEP, CET);
  not not_2 (not_2_out, LE);
  and and_2 (and_2_out, D1, not_2_out);
  and and_3 (and_3_out, Q1, LE);
  and and_4 (and_4_out, D2, not_2_out);
  and and_5 (and_5_out, Q2, LE);
  and and_6 (and_6_out, Q1, and_1_out);
  and and_7 (and_7_out, D3, not_2_out);
  and and_8 (and_8_out, Q3, LE);
  and and_9 (and_9_out, Q2, Q1, and_1_out);
  and and_10 (and_10_out, D4, not_2_out);
  and and_11 (and_11_out, Q4, LE);
  and and_12 (and_12_out, Q3, Q2, Q1, and_1_out);
  xor xor_1 (xor_1_out, and_3_out, and_1_out);
  xor xor_2 (xor_2_out, and_5_out, and_6_out);
  xor xor_3 (xor_3_out, and_8_out, and_9_out);
  xor xor_4 (xor_4_out, and_11_out, and_12_out);
  or or_1 (or_1_out, and_2_out, xor_1_out);
  or or_2 (or_2_out, and_4_out, xor_2_out);
  or or_3 (or_3_out, and_7_out, xor_3_out);
  or or_4 (or_4_out, and_10_out, xor_4_out);
  // D_Flip_Flop d_flip_flop_1: pin names not known; wires that end beside it: or_1_out, CLK, not_1_out, Q1
  // D_Flip_Flop d_flip_flop_2: pin names not known; wires that end beside it: or_2_out, CLK, not_1_out, Q2
  // D_Flip_Flop d_flip_flop_3: pin names not known; wires that end beside it: or_3_out, CLK, not_1_out, Q3
  // D_Flip_Flop d_flip_flop_4: pin names not known; wires that end beside it: or_4_out, CLK, not_1_out, Q4
  and and_13 (TC, Q4, Q3, Q2, Q1, CET);
endmodule

module _74574_Peek (
  input  nOE,
  input  CLK,
  input  [7:0] D,
  output [7:0] P,
  output [7:0] Q
);

  wire not_1_out;

  not not_1 (not_1_out, nOE);
  // D_Flip_Flop d_flip_flop_1: pin names not known; wires that end beside it: D[0], P[0]
  // D_Flip_Flop d_flip_flop_2: pin names not known; wires that end beside it: CLK, D[1], P[1]
  // D_Flip_Flop d_flip_flop_3: pin names not known; wires that end beside it: CLK, D[2], P[2]
  // D_Flip_Flop d_flip_flop_4: pin names not known; wires that end beside it: CLK, D[3], CLK, P[3]
  // D_Flip_Flop d_flip_flop_5: pin names not known; wires that end beside it: D[4], CLK, P[4]
  // D_Flip_Flop d_flip_flop_6: pin names not known; wires that end beside it: D[5], P[5]
  // D_Flip_Flop d_flip_flop_7: pin names not known; wires that end beside it: CLK, D[6], P[6]
  // D_Flip_Flop d_flip_flop_8: pin names not known; wires that end beside it: CLK, D[7], CLK, P[7]
  assign Q[0] = not_1_out ? P[0] : 1'bz;  // Controlled_Buffer controlled_buffer_1
  assign Q[1] = not_1_out ? P[1] : 1'bz;  // Controlled_Buffer controlled_buffer_2
  assign Q[2] = not_1_out ? P[2] : 1'bz;  // Controlled_Buffer controlled_buffer_3
  assign Q[3] = not_1_out ? P[3] : 1'bz;  // Controlled_Buffer controlled_buffer_4
  assign Q[4] = not_1_out ? P[4] : 1'bz;  // Controlled_Buffer controlled_buffer_5
  assign Q[5] = not_1_out ? P[5] : 1'bz;  // Controlled_Buffer controlled_buffer_6
  assign Q[6] = not_1_out ? P[6] : 1'bz;  // Controlled_Buffer controlled_buffer_7
  assign Q[7] = not_1_out ? P[7] : 1'bz;  // Controlled_Buffer controlled_buffer_8
endmodule
